# Fritzing sketch humanoid robot (saved by Fritzing 0.9.3b)

parts:
  U1 = LIPO-1000mAh [package=lipo-1000]
  S1 = Round Pushbutton
  LM1 = RioRand LM2596
  LM2 = RioRand LM2596
  Part1 = Arduino Motor Shield
  LM3 = RioRand LM2596
  J1 = Basic Servo  # not connected
  J2 = Basic Servo  # not connected
  J3 = Basic Servo  # not connected
  J4 = Basic Servo  # not connected
  J5 = Basic Servo  # not connected
  J6 = Basic Servo  # not connected
  J7 = Basic Servo
  J8 = Basic Servo
  J9 = Basic Servo
  J10 = Basic Servo
  J11 = Basic Servo
  J12 = Basic Servo
  Part2 = Arduino Nano (Rev3.0)
  Part3 = Arduino Nano (Rev3.0)
  Part4 = Bluetooth HC-05 Macho
  LED1 = smd LED [color="Red (633nm)" package="1206 [SMD]"]
  LED2 = smd LED [color="Red (633nm)" package="1206 [SMD]"]
  LED3 = smd LED [color="Red (633nm)" package="1206 [SMD]"]
  LED4 = smd LED [color="Red (633nm)" package="1206 [SMD]"]
  R1 = Resistor [tolerance=±5% resistance=220 package="0603 [SMD]"]
  R2 = Resistor [tolerance=±5% resistance=220 package="0603 [SMD]"]
  M1 = DC Motor  # not connected
  M2 = DC Motor  # not connected
  WeMos_D1_Mini_Relay_Shield_V1 = WeMos D1 Mini Relay Shield V2
  WeMos_D1_Mini_Relay_Shield_V2 = WeMos D1 Mini Relay Shield V2
  LM4 = RioRand LM2596
  J13 = Basic Servo
  J14 = Basic Servo

nets:
  N1: U1.+, S1.leg0, R2.Pin_1
  N2: U1.-, Part1.GND, R2.Pin_0
  N3: S1.leg1, Part1.VIN
  VCC: LM1.Pin_2, J7.vcc, J9.vcc
  N4: LM1.Pin_3, J7.gnd
  N5: LM2.Pin_2, J12.vcc
  N6: LM2.Pin_3, J12.gnd
  N7: Part1.A0, Part2.D10
  N8: Part1.A1, Part2.D9
  N9: Part1.A2, Part2.D8
  N10: Part1.A3, Part2.D7
  N11: Part1.A4, Part2.D6
  N12: Part1.A5, Part2.D5
  VIN: LM3.Pin_2, Part2.VIN, Part3.VIN
  GND: LM3.Pin_3, Part2.GND, Part3.GND, Part4.GND, LED2.cathode, LED3.cathode, LED4.cathode
  N13: J7.pulse, Part3.D9
  N14: J8.pulse, Part3.D8
  N15: J9.pulse, Part3.D7
  N16: J10.pulse, Part3.D6
  N17: J11.pulse, Part3.D5
  N18: J12.pulse, Part3.D4
  N19: Part2.D1/TX, Part3.D0/RX
  N20: Part2.D0/RX, Part3.D1/TX
  N21: Part2.D2, Part4.TXD
  N22: Part2.D3, Part4.RXD
  N23: Part2.D11/MOSI, WeMos_D1_Mini_Relay_Shield_V1.D6
  5V: Part2.5V, Part4.VCC, WeMos_D1_Mini_Relay_Shield_V1.3V3
  N24: Part2.A4, LED4.anode
  N25: Part2.A3, LED3.anode
  N26: Part2.A2, LED1.anode
  N27: Part2.A1, LED2.anode
  N28: Part2.A0, R1.Pin_1
  N29: Part3.D10, J13.pulse
  N30: Part3.D11/MOSI, J14.pulse
  N31: WeMos_D1_Mini_Relay_Shield_V1.RX, WeMos_D1_Mini_Relay_Shield_V2.A0, LM4.Pin_2
  N32: WeMos_D1_Mini_Relay_Shield_V1.TX, WeMos_D1_Mini_Relay_Shield_V2.RST, LM4.Pin_3

notes:
  Feszültség osztó táp feszültség méréshez
  Akku állapot visszajelző ledek.
  Servo és Arduino közötti kapcsolat egy interface nyákon keresztül történik.
  Fej mozgató servo
  2 utas relay modul külön sep-down converterrel a relay switch táplálásához. A Servo step-down modulok tápjának k, be kapcsolására.
  A 2 Arduino tápját adó Step-down.
  Kar mozgató servo tápot szolgáltató step Down
  HC 12 433 Mhz es trasciever.
